# Fritzing sketch pi3-temperature-sensor (saved by Fritzing 0.9.3b)
breadboards: 1

parts:
  Raspberry_Pi_1 = Raspberry Pi 3 [part_number=RPI-3-V1.2]
  LED1 = RGB LED (com. cathode, rgb) [package="5 mm [THT]"]
  R1 = Resistor [tolerance=±5% resistance=220 package="0805 [SMD]"]
  R2 = Resistor [tolerance=±5% resistance=220 package=THT]  # not connected
  R3 = Resistor [tolerance=±5% resistance=47k package="0402 [SMD]"]
  R4 = Resistor [tolerance=±5% resistance=220 package="0805 [SMD]"]
  R5 = Resistor [tolerance=±5% resistance=220 package="0805 [SMD]"]
  DS1 = DS18B20 1-Wire Temperature Sensor [part_number=DS18B20]

nets:
  3V3: Raspberry_Pi_1.3v3, R3.Pin_0, DS1.VDD
  N1: Raspberry_Pi_1.GPIO4, DS1.DQ
  N2: Raspberry_Pi_1.GPIO17, LED1.red_anode, R1.Pin_0, R1.Pin_1
  N3: Raspberry_Pi_1.GPIO27, LED1.blue_anode, R5.Pin_0, R5.Pin_1
  GND: Raspberry_Pi_1.GND, LED1.common_cathode, DS1.GND
  N4: Raspberry_Pi_1.GPIO18, LED1.green_anode, R4.Pin_0, R4.Pin_1
